// Logisim project ALU.circ as structural Verilog: 1 circuit, main circuit ALU
module ALU (
  input  [31:0] A,
  input  [31:0] in_2,
  input  [31:0] B,
  input  [4:0] Shift,
  input  CarryIn,
  input  [3:0] Codop,
  output [3:0] Flags,
  output [31:0] S
);

  wire [31:0] AandB, AmBpCm1, AorB, ApB, ApBpC, AxB, AxorB, BandnA, Blshift, BmA, Brashift, Brrshift,
       Brshift, nA, not_1_out, undriven, ZmA;

  assign AandB = A & B;  // AND_Gate and_1, 32 bits wide
  assign AxorB = A ^ B;  // XOR_Gate xor_1, 32 bits wide
  Shifter #(.width(32)) shifter_1 (.in(B), .\dist (Shift), .out(Blshift));
  Shifter #(.shift("lr"), .width(32)) shifter_2 (.in(B), .\dist (Shift), .out(Brshift));
  Shifter #(.shift("ar"), .width(32)) shifter_3 (.in(B), .\dist (Shift), .out(Brashift));
  Adder #(.width(32)) adder_1 (.a(A), .b(B), .out(ApBpC), .cin(CarryIn));  // open: cout
  Subtractor #(.width(32)) subtractor_1 (.a(A), .b(B), .out(AmBpCm1), .bin(CarryIn));  // open: bout
  Shifter #(.shift("rr"), .width(32)) shifter_4 (.in(B), .\dist (Shift), .out(Brrshift));
  // AND_Gate and_2 has open pins: in0=A, in1=B, out=open
  assign not_1_out = ~A;  // NOT_Gate not_1, 32 bits wide
  Subtractor #(.width(32)) subtractor_2 (.a(in_2), .b(A), .out(ZmA));  // open: bin, bout
  Subtractor #(.width(32)) subtractor_3 (.a(B), .b(A), .out(BmA));  // open: bin, bout
  Adder #(.width(32)) adder_2 (.a(A), .b(B), .out(ApB));  // open: cin, cout
  Multiplier #(.width(32)) multiplier_1 (.a(A), .b(B), .out(AxB));  // open: cin, cout
  assign AorB = A | B;  // OR_Gate or_1, 32 bits wide
  assign BandnA = B & not_1_out;  // AND_Gate and_3, 32 bits wide
  assign nA = ~A;  // NOT_Gate not_2, 32 bits wide
  Multiplexer #(.select(4), .width(32)) multiplexer_1 (
    .in0(AandB), .in1(AxorB), .in2(Blshift), .in3(Brshift), .in4(Brashift), .in5(ApBpC), .in6(AmBpCm1),
    .in7(Brrshift), .in8(undriven), .in9(ZmA), .in10(BmA), .in11(ApB), .in12(AorB), .in13(AxB),
    .in14(BandnA), .in15(nA), .out(S), .sel(Codop));

  // Other names for the same wires on the sheet: CI = CarryIn; Flag[3:0] = Flags
endmodule
